# Fritzing sketch optical (saved by Fritzing 0.8.7b)
breadboards: 1

parts:
  元件1 = Arduino Uno (Rev3) - ICSP
  J1 = Piezo Speaker
  R1 = Resistor [tolerance=±5% resistance=10k package=THT]
  R2 = Photocell (LDR) [package=THT]

nets:
  N1: 元件1.A0, R1.Pin_0, R2.pin_1
  N2: 元件1.D9_PWM, J1.pin2
  N3: 元件1.GND, J1.pin1, R1.Pin_1
  N4: 元件1.5V, R2.pin_0
