# Fritzing sketch flame sensor (saved by Fritzing 0.8.7b)

parts:
  module1 = Flame Sensor-V1.0
  元件1 = Arduino Uno (Rev3) - ICSP

nets:
  N1: module1.AO, 元件1.A0
  N2: module1.DO, 元件1.D8
  N3: module1.+, 元件1.5V
  N4: module1.G, 元件1.GND

notes:
  Flame Sensor

custom parts:
  Flame Sensor-V1.0: Flame Sensor V1.0 module of SunFounder Sensor Kit
