# Fritzing sketch voltmeter (saved by Fritzing 0.8.7b)
breadboards: 1

parts:
  module1 = I2C LCD1602
  元件1 = Arduino Uno (Rev3) - ICSP
  R1 = Rotary Potentiometer (Small) [maximum_resistance=100kΩ package=THT]

nets:
  N1: module1.SCL, 元件1.A5/SCL
  N2: module1.SDA, 元件1.A4/SDA
  VCC: module1.VCC, 元件1.5V, R1.leg2
  GND: module1.GND, 元件1.GND, R1.leg1
  N3: 元件1.A0, R1.wiper

notes:
  I2C LCD1602

custom parts:
  I2C LCD1602: I2C LCD1602 module of SunFounder Sensor Kit
