# Fritzing sketch voice sensor (saved by Fritzing 0.8.7b)

parts:
  元件1 = Arduino Uno (Rev3) - ICSP
  module1 = sound sensor-v1.0

nets:
  N1: 元件1.A0, module1.A0
  N2: 元件1.D8, module1.D0
  N3: 元件1.5V, module1.+
  N4: 元件1.GND, module1.G

notes:
  Voice Sensor

custom parts:
  sound sensor-v1.0: sound sensor-v1.0 module
