# Fritzing sketch LM35 Temperature Sensor (saved by Fritzing 0.8.7b)
breadboards: 1

parts:
  元件1 = Arduino Uno (Rev3) - ICSP
  module1 = I2C LCD1602
  T1 = LM35 Temperature Sensor [package="TO92 [THT]"]

nets:
  N1: 元件1.A0, T1.Vout
  N2: 元件1.A4/SDA, module1.SDA
  N3: 元件1.A5/SCL, module1.SCL
  GND: 元件1.GND, module1.GND, T1.GND
  5V: 元件1.5V, module1.VCC, T1.+Vs

notes:
  I2C LCD1602

custom parts:
  I2C LCD1602: I2C LCD1602 module of SunFounder Sensor Kit
