# Fritzing sketch Water Level Sensor (saved by Fritzing 0.8.7b)
breadboards: 1

parts:
  元件1 = Arduino Uno (Rev3) - ICSP
  module1 = I2C LCD1602
  module2 = Water sensor

nets:
  N1: 元件1.A0, module2.S
  N2: 元件1.A4/SDA, module1.SDA
  N3: 元件1.A5/SCL, module1.SCL
  GND: 元件1.GND, module1.GND, module2.-
  5V: 元件1.5V, module1.VCC, module2.+

notes:
  Water level sensor
  I2C LCD1602

custom parts:
  I2C LCD1602: I2C LCD1602 module of SunFounder Sensor Kit
  Water sensor: Water sensor module of SunFounder Sensor Kit
