# Fritzing sketch Dot-matrix (saved by Fritzing 0.8.7b)
breadboards: 1

parts:
  U1 = 74HC595 SMD [package="SO16 [SMD]"]
  U2 = 74HC595 [package="DIP16 [THT]"]
  R1 = Resistor [tolerance=±5% resistance=220 package=THT]
  R2 = Resistor [tolerance=±5% resistance=220 package=THT]
  R3 = Resistor [tolerance=±5% resistance=220 package=THT]
  R4 = Resistor [tolerance=±5% resistance=220 package=THT]
  R5 = Resistor [tolerance=±5% resistance=220 package=THT]
  R6 = Resistor [tolerance=±5% resistance=220 package=THT]
  R7 = Resistor [tolerance=±5% resistance=220 package=THT]
  R8 = Resistor [tolerance=±5% resistance=220 package=THT]
  元件1 = Arduino Uno (Rev3) - ICSP
  module1 = 788BS Dot matix

nets:
  N1: U1.Q1, R6.Pin_1
  N2: U1.Q2, R1.Pin_1
  N3: U1.Q3, R4.Pin_1
  N4: U1.Q4, R3.Pin_1
  N5: U1.Q5, R2.Pin_1
  N6: U1.Q6, R5.Pin_1
  N7: U1.Q7, R8.Pin_1
  GND: U1.GND, U1.OE, U2.GND, 元件1.GND
  VCC: U1.MR, U1.VCC, U2.MR, U2.VCC, 元件1.5V
  N8: U1.SH_CP, U2.SH_CP, 元件1.ICSP_MISO, 元件1.D12/MISO
  N9: U1.ST_CP, U2.ST_CP, 元件1.D8
  N10: U1.DS, U2.Q7'
  N11: U1.Q0, R7.Pin_1
  N12: U2.Q1, module1.P3
  N13: U2.Q2, module1.P4
  N14: U2.Q3, module1.P10
  N15: U2.Q4, module1.P6
  N16: U2.Q5, module1.P11
  N17: U2.Q6, module1.P15
  N18: U2.Q7, module1.P16
  N19: U2.DS, 元件1.ICSP_MOSI, 元件1.D11_PWM/MOSI
  N20: U2.Q0, module1.P13
  N21: R1.Pin_0, module1.P7
  N22: R2.Pin_0, module1.P8
  N23: R3.Pin_0, module1.P12
  N24: R4.Pin_0, module1.P1
  N25: R5.Pin_0, module1.P14
  N26: R6.Pin_0, module1.P2
  N27: R7.Pin_0, module1.P5
  N28: R8.Pin_0, module1.P9

custom parts:
  788BS Dot matix: 788BS 8x8 dot matix from SunFounder
