# Fritzing sketch rgb (saved by Fritzing 0.8.7b)

parts:
  module1 = rgb-v1.0
  元件1 = Arduino Uno (Rev3) - ICSP

nets:
  N1: module1.R, 元件1.ICSP_MOSI, 元件1.D11_PWM/MOSI
  N2: module1.G, 元件1.D10_PWM/SS
  N3: module1.B, 元件1.D9_PWM
  N4: module1.-, 元件1.GND

notes:
  RGB LED

custom parts:
  rgb-v1.0: rgb-v1.0 module of SunFounder Sensor Kit
