# Fritzing sketch 74hc595 (saved by Fritzing 0.8.7b)
breadboards: 1

parts:
  U1 = 74HC595 [package="DIP16 [THT]"]
  DI1 = 7-Segment LED Display [package=THT]
  R8 = Resistor [tolerance=±5% resistance=220 package=THT]
  R6 = Resistor [tolerance=±5% resistance=220 package=THT]
  R1 = Resistor [tolerance=±5% resistance=220 package=THT]
  R4 = Resistor [tolerance=±5% resistance=220 package=THT]
  R2 = Resistor [tolerance=±5% resistance=220 package=THT]
  R7 = Resistor [tolerance=±5% resistance=220 package=THT]
  R5 = Resistor [tolerance=±5% resistance=220 package=THT]
  R3 = Resistor [tolerance=±5% resistance=220 package=THT]
  元件1 = Arduino Uno (Rev3) - ICSP

nets:
  N1: U1.Q1, R3.Pin_0
  N2: U1.Q2, R5.Pin_0
  N3: U1.Q3, R2.Pin_0
  N4: U1.Q4, R1.Pin_0
  N5: U1.Q5, R8.Pin_1
  N6: U1.Q6, R7.Pin_1
  N7: U1.Q7, R4.Pin_1
  GND: U1.GND, U1.OE, DI1.commAnode#2, 元件1.GND
  VCC: U1.MR, U1.VCC, 元件1.5V
  N8: U1.SH_CP, 元件1.D8
  N9: U1.ST_CP, 元件1.ICSP_MISO, 元件1.D12/MISO
  N10: U1.DS, 元件1.ICSP_MOSI, 元件1.D11_PWM/MOSI
  N11: U1.Q0, R6.Pin_1
  N12: DI1.cathodeE, R2.Pin_1
  N13: DI1.cathodeD, R1.Pin_1
  N14: DI1.cathodeC, R8.Pin_0
  N15: DI1.cathodeDP, R6.Pin_0
  N16: DI1.cathodeB, R7.Pin_0
  N17: DI1.cathodeA, R4.Pin_0
  N18: DI1.cathodeF, R5.Pin_1
  N19: DI1.cathodeG, R3.Pin_1
