# Fritzing sketch button (saved by Fritzing 0.8.7b)

parts:
  元件1 = Arduino Uno (Rev3) - ICSP
  S1 = button module v1.0 [package=THT]

nets:
  N1: 元件1.D8, S1.S
  N2: 元件1.5V, S1.+
  N3: 元件1.GND, S1.-

notes:
  Button Module

custom parts:
  button module v1.0: button module www.sunfounder.com
