# Fritzing sketch Humiture Sensor (saved by Fritzing 0.8.7b)
breadboards: 1

parts:
  module1 = I2C LCD1602
  S1 = Humiture Sensor v1.0 [package=THT]
  元件1 = Arduino Uno (Rev3) - ICSP

nets:
  N1: module1.SCL, 元件1.A5/SCL
  N2: module1.SDA, 元件1.A4/SDA
  VCC: module1.VCC, S1.+, 元件1.5V
  GND: module1.GND, S1.-, 元件1.GND
  N3: S1.S, 元件1.D4

notes:
  Humiture Sensor
  I2C LCD1602

custom parts:
  I2C LCD1602: I2C LCD1602 module of SunFounder Sensor Kit
  Humiture Sensor v1.0: Humiture Sensor www.sunfounder.com
