# Fritzing sketch relay (saved by Fritzing 0.8.7b)

parts:
  module1 = relay -v1.0 module
  元件1 = Arduino Uno (Rev3) - ICSP

nets:
  N1: module1.S, 元件1.D8
  N2: module1.+, 元件1.5V
  N3: module1.-, 元件1.GND

notes:
  Relay Module

custom parts:
  relay -v1.0 module: relay v1.0 module from SunFounder Sensor Kit
