# Fritzing sketch Joystick PS2 (saved by Fritzing 0.8.7b)

parts:
  元件1 = Arduino Uno (Rev3) - ICSP
  module1 = joystick PS2-v1.0

nets:
  N1: 元件1.A0, module1.VRX
  N2: 元件1.A1, module1.VRY
  N3: 元件1.D8, module1.SW
  5V: 元件1.5V, module1.VCC
  GND: 元件1.GND, module1.GND

notes:
  Joystick PS2

custom parts:
  joystick PS2-v1.0: joystick ps2 module of SunFounder Sensor Kit
