# Fritzing sketch ir-receiver (saved by Fritzing 0.8.7b)

parts:
  元件1 = Arduino Uno (Rev3) - ICSP
  module1 = Ir Receiver-v1.0

nets:
  N1: 元件1.D2, module1.Y
  N2: 元件1.5V, module1.R
  N3: 元件1.GND, module1.G

notes:
  IR-Receiver

custom parts:
  Ir Receiver-v1.0: Infrared-Receiver module of SunFounder Sensor Kit
