# Fritzing sketch Password Lock (saved by Fritzing 0.8.7b)
breadboards: 1

parts:
  元件1 = Arduino Uno (Rev3) - ICSP
  module2 = Relay Module
  U1 = KeyPad [package=DIP8]
  module3 = I2C LCD1602

nets:
  N1: 元件1.A4/SDA, module3.SDA
  N2: 元件1.A5/SCL, module3.SCL
  N3: 元件1.ICSP_MOSI, 元件1.D11_PWM/MOSI, U1.connector4
  VCC: 元件1.5V, module2.VCC, module3.VCC
  GND: 元件1.GND, module2.GND, module3.GND
  N4: 元件1.D8, U1.connector7
  N5: 元件1.D9_PWM, U1.connector6
  N6: 元件1.D10_PWM/SS, U1.connector5
  N7: 元件1.D13/SCK, module2.SIG
  N8: 元件1.D4, U1.connector3
  N9: 元件1.D5_PWM, U1.connector2
  N10: 元件1.D6_PWM, U1.connector1
  N11: 元件1.D7, U1.connector0

notes:
  KeyPad
  relay

custom parts:
  Relay Module: Relay Module of SunFounder Sensor Kit
  KeyPad: 4x4 KeyPad
  I2C LCD1602: I2C LCD1602 module of SunFounder Sensor Kit
